// Logisim project NearExact.circ as structural Verilog: 9 circuits, main circuit main
module main (
);

  wire ALU_carryflag, ALU_zeroflag, and_1_out, and_2_out, and_4_out, and_5_out, MainClock_clk,
       ModeSelect_sw1, ModeSelect_sw2, not_1_out, or_1_out, or_2_out, Pulse_out, Reset_out;
  wire [2:0] rom_2_data_2, rom_3_data_2, rom_4_data_2;
  wire [3:0] Address_2_toram, Address_sw4, rom_2_data, rom_3_data, rom_4_data;
  wire [6:0] Instruction_tosignalrom;
  wire [7:0] AReg_toalu, BReg_toalu, Data_sw8, MainRAM_data;
  wire [8:0] Output_out;
  wire [16:0] and_3_out, bit_extender_1_out, rom_1_data;

  DipSwitch #(.number(2)) ModeSelect (.sw1(ModeSelect_sw1), .sw2(ModeSelect_sw2));
  Button Pulse (.out(Pulse_out));
  Button Reset (.out(Reset_out));
  or or_1 (or_1_out, ModeSelect_sw2, and_3_out[13]);
  DipSwitch #(.number(4)) Address (
    .sw1(Address_sw4[3]), .sw2(Address_sw4[2]), .sw3(Address_sw4[1]), .sw4(Address_sw4[0]));
  DipSwitch Data (
    .sw1(Data_sw8[7]), .sw2(Data_sw8[6]), .sw3(Data_sw8[5]), .sw4(Data_sw8[4]), .sw5(Data_sw8[3]),
    .sw6(Data_sw8[2]), .sw7(Data_sw8[1]), .sw8(Data_sw8[0]));
  CPUClock MainClock (.Clk(MainClock_clk), .Pulse(Pulse_out), .StepMode(ModeSelect_sw1), .Halt(and_3_out[15]));
  RAM #(.addrWidth(4), .databus("bidir")) MainRAM (.addr(Address_2_toram), .data(MainRAM_data));  // open: we, oe, clk
  AddrRegister Address_2 (
    .ToRAM(Address_2_toram), .ProgramMode(ModeSelect_sw2), .AddrBypass(Address_sw4), .D(MainRAM_data),
    .WriteEnable(and_3_out[14]), .Clock(MainClock_clk), .Reset(Reset_out));
  assign MainRAM_data = ModeSelect_sw1 ? Data_sw8 : 8'bz;  // Controlled_Buffer controlled_buffer_1
  not not_1 (not_1_out, ModeSelect_sw1);
  InstructionFetcher Instruction (
    .ToSignalROM(Instruction_tosignalrom), .ToBus(MainRAM_data), .IRWriteEnable(and_3_out[10]),
    .InstructionIn(MainRAM_data), .ReadEnable(and_3_out[11]), .Clock(and_1_out), .Reset(Reset_out));
  // Probe on MainRAM_data
  ProgramCounter PC (
    .ToBus(MainRAM_data), .D(MainRAM_data), .Reset(Reset_out), .Clock(MainClock_clk),
    .WriteEnable(and_3_out[3]), .LoadEnable(or_2_out), .ReadEnable(and_3_out[2]));
  ARegister AReg (
    .ToBus(MainRAM_data), .ToALU(AReg_toalu), .D(MainRAM_data), .ReadEnable(and_3_out[8]), .Reset(Reset_out),
    .Clock(MainClock_clk), .WriteEnable(and_3_out[9]));
  BRegister BReg (
    .ToALU(BReg_toalu), .D(MainRAM_data), .Reset(Reset_out), .Clock(MainClock_clk), .WriteEnable(and_3_out[5]));
  Output Output (
    .Out(Output_out[7:0]), .D(MainRAM_data), .Reset(Reset_out), .Clock(MainClock_clk),
    .WriteEnable(and_3_out[4]));
  and and_1 (and_1_out, not_1_out, MainClock_clk);
  ROM #(.addrWidth(7), .dataWidth(17)) rom_1 (.addr(Instruction_tosignalrom), .data(rom_1_data));
  Pull_Resistor pull_resistor_1 (.node(MainRAM_data));
  ALU ALU (
    .ZeroFlag(ALU_zeroflag), .ToBus(MainRAM_data), .CarryFlag(ALU_carryflag), .A(AReg_toalu), .B(BReg_toalu),
    .Subtract(and_3_out[6]), .AddEnable(and_3_out[7]), .Clock(MainClock_clk), .Reset(Reset_out));
  and and_2 (and_2_out, ALU_zeroflag, and_3_out[16]);
  assign and_3_out = rom_1_data & bit_extender_1_out;  // AND_Gate and_3, 17 bits wide
  assign bit_extender_1_out = {{16{not_1_out}}, not_1_out};  // Bit_Extender bit_extender_1
  or or_2 (or_2_out, and_3_out[1], and_2_out, and_4_out);
  and and_4 (and_4_out, ALU_carryflag, and_3_out[0]);
  DipSwitch #(.number(2)) Signed (.sw1(Output_out[8]));  // open: sw2
  and and_5 (and_5_out, Output_out[7], Output_out[8]);
  _7_Segment_Display u_7_segment_display_1 (
    .g(and_5_out), .f(1'b0), .a(1'b0), .b(1'b0), .e(1'b0), .d(1'b0), .c(1'b0), .dp(1'b0));
  ROM #(.addrWidth(9), .dataWidth(7)) rom_2 (.addr(Output_out), .data({rom_2_data_2, rom_2_data}));
  ROM #(.addrWidth(9), .dataWidth(7)) rom_3 (.addr(Output_out), .data({rom_3_data_2, rom_3_data}));
  ROM #(.addrWidth(9), .dataWidth(7)) rom_4 (.addr(Output_out), .data({rom_4_data_2, rom_4_data}));
  _7_Segment_Display u_7_segment_display_2 (
    .g(rom_2_data[3]), .f(rom_2_data[2]), .a(rom_2_data[1]), .b(rom_2_data[0]), .e(rom_2_data_2[2]),
    .d(rom_2_data_2[1]), .c(rom_2_data_2[0]), .dp(1'b0));
  _7_Segment_Display u_7_segment_display_3 (
    .g(rom_3_data[3]), .f(rom_3_data[2]), .a(rom_3_data[1]), .b(rom_3_data[0]), .e(rom_3_data_2[2]),
    .d(rom_3_data_2[1]), .c(rom_3_data_2[0]), .dp(1'b0));
  _7_Segment_Display u_7_segment_display_4 (
    .g(rom_4_data[3]), .f(rom_4_data[2]), .a(rom_4_data[1]), .b(rom_4_data[0]), .e(rom_4_data_2[2]),
    .d(rom_4_data_2[1]), .c(rom_4_data_2[0]), .dp(1'b0));

  // Notes on the sheet:
  //    Instruction Set
  //   0000	0x	NOP
  //   0001	1x	LDA
  //   0010	2x	ADD
  //   0011	3x	SUB
  //   0100	4x	STA
  //   0101	5x	LDI
  //   0110	6x	JMP
  //   0111	7x	JC
  //   1000	8x	JZ
  //   1001	9x	
  //   1010	Ax	
  //   1011	Bx	
  //   1100	Cx	
  //   1101	Dx	
  //   1110	Ex	OUT
  //   1111	Fx	HLT
  //   contents of rom_1 (hex, n*v repeats v):
  //   4004 1408 6*0 4004 1408 4800 1200 0 0 0 1 4004 1408 4800 1020 280 0 0 2 4004 1408 4800 1020 2c0 0 0
  //   3 4004 1408 4800 2100 0 0 0 4 4004 1408 a00 4*0 5 4004 1408 802 4*0 6 4004 1408 801 4*0 7 4004 1408
  //   10800 4*0 8 4004 1408 5*0 9 4004 1408 5*0 a 4004 1408 5*0 b 4004 1408 5*0 c 4004 1408 5*0 d 4004
  //   1408 110 4*0 e 4004 1408 18000 4*0 f
  //   contents of rom_2 (hex, n*v repeats v):
  //   100*0 100*11 56*6b 100*0 57*11
  //   contents of rom_3 (hex, n*v repeats v):
  //   10*0 10*11 10*6b 10*3b 10*1d 10*3e 10*7e 10*17 10*7f 10*3f 10*77 10*11 10*6b 10*3b 10*1d 10*3e 10*7e
  //   10*17 10*7f 10*3f 10*77 10*11 10*6b 10*3b 10*1d 6*3e 10*0 10*11 10*6b 10*3b 10*1d 10*3e 10*7e 10*17
  //   10*7f 10*3f 10*77 10*11 17*6b 10*11 10*77 10*3f 10*7f 10*17 10*7e 10*3e 10*1d 10*3b 10*6b 10*11
  //   contents of rom_4 (hex, n*v repeats v):
  //   77 11 6b 3b 1d 3e 7e 17 7f 3f 77 11 6b 3b 1d 3e 7e 17 7f 3f 77 11 6b 3b 1d 3e 7e 17 7f 3f 77 11 6b
  //   3b 1d 3e 7e 17 7f 3f 77 11 6b 3b 1d 3e 7e 17 7f 3f 77 11 6b 3b 1d 3e 7e 17 7f 3f 77 11 6b 3b 1d 3e
  //   7e 17 7f 3f 77 11 6b 3b 1d 3e 7e 17 7f 3f 77 11 6b 3b 1d 3e 7e 17 7f 3f 77 11 6b 3b 1d 3e 7e 17 7f
  //   3f 77 11 6b 3b 1d 3e 7e 17 7f 3f 77 11 6b 3b 1d 3e 7e 17 7f 3f 77 11 6b 3b 1d 3e 7e 17 7f 3f 77 11
  //   6b 3b 1d 3e 7e 17 7f 3f 77 11 6b 3b 1d 3e 7e 17 7f 3f 77 11 6b 3b 1d 3e 7e 17 7f 3f 77 11 6b 3b 1d
  //   3e 7e 17 7f 3f 77 11 6b 3b 1d 3e 7e 17 7f 3f 77 11 6b 3b 1d 3e 7e 17 7f 3f 77 11 6b 3b 1d 3e 7e 17
  //   7f 3f 77 11 6b 3b 1d 3e 7e 17 7f 3f 77 11 6b 3b 1d 3e 7e 17 7f 3f 77 11 6b 3b 1d 3e 7e 17 7f 3f 77
  //   11 6b 3b 1d 3e 7e 17 7f 3f 77 11 6b 3b 1d 3e 7e 17 7f 3f 77 11 6b 3b 1d 3e 77 11 6b 3b 1d 3e 7e 17
  //   7f 3f 77 11 6b 3b 1d 3e 7e 17 7f 3f 77 11 6b 3b 1d 3e 7e 17 7f 3f 77 11 6b 3b 1d 3e 7e 17 7f 3f 77
  //   11 6b 3b 1d 3e 7e 17 7f 3f 77 11 6b 3b 1d 3e 7e 17 7f 3f 77 11 6b 3b 1d 3e 7e 17 7f 3f 77 11 6b 3b
  //   1d 3e 7e 17 7f 3f 77 11 6b 3b 1d 3e 7e 17 7f 3f 77 11 6b 3b 1d 3e 7e 17 7f 3f 77 11 6b 3b 1d 3e 7e
  //   17 7f 3f 77 11 6b 3b 1d 3e 7e 17 7f 3f 77 11 6b 3b 1d 3e 7e 17 7f 17 7e 3e 1d 3b 6b 11 77 3f 7f 17
  //   7e 3e 1d 3b 6b 11 77 3f 7f 17 7e 3e 1d 3b 6b 11 77 3f 7f 17 7e 3e 1d 3b 6b 11 77 3f 7f 17 7e 3e 1d
  //   3b 6b 11 77 3f 7f 17 7e 3e 1d 3b 6b 11 77 3f 7f 17 7e 3e 1d 3b 6b 11 77 3f 7f 17 7e 3e 1d 3b 6b 11
  //   77 3f 7f 17 7e 3e 1d 3b 6b 11 77 3f 7f 17 7e 3e 1d 3b 6b 11 77 3f 7f 17 7e 3e 1d 3b 6b 11 77 3f 7f
  //   17 7e 3e 1d 3b 6b 11 77 3f 7f 17 7e 3e 1d 3b 6b 11
endmodule

module ARegister (
  input  [7:0] D,
  input  ReadEnable,
  input  Reset,
  input  Clock,
  input  WriteEnable,
  output [7:0] ToALU,
  output [7:0] ToBus
);

  Register RegA (.D(D), .en(WriteEnable), .Q(ToALU), .clk(Clock), .clr(Reset));
  assign ToBus = ReadEnable ? ToALU : 8'bz;  // Controlled_Buffer controlled_buffer_1
endmodule

module BRegister (
  input  [7:0] D,
  input  Reset,
  input  Clock,
  input  WriteEnable,
  output [7:0] ToALU
);

  Register RegB (.D(D), .en(WriteEnable), .Q(ToALU), .clk(Clock), .clr(Reset));
endmodule

module ALU (
  input  Subtract,
  input  [7:0] A,
  input  [7:0] B,
  input  AddEnable,
  input  Clock,
  input  Reset,
  output ZeroFlag,
  output CarryFlag,
  output [7:0] ToBus
);

  wire adder_1_cout, comparator_1_eq, xor_2_out;
  wire [7:0] adder_1_out, bit_extender_1_out, xor_1_out;

  assign bit_extender_1_out = {{7{Subtract}}, Subtract};  // Bit_Extender bit_extender_1
  Adder adder_1 (.a(A), .b(xor_1_out), .out(adder_1_out), .cin(Subtract), .cout(adder_1_cout));
  assign xor_1_out = bit_extender_1_out ^ B;  // XOR_Gate xor_1, 8 bits wide
  xor xor_2 (xor_2_out, Subtract, adder_1_cout);
  assign ToBus = AddEnable ? adder_1_out : 8'bz;  // Controlled_Buffer controlled_buffer_1
  D_Flip_Flop #(.enable("true")) d_ff_1 (
    .clk(Clock), .D(xor_2_out), .Q(CarryFlag), .preset(1'b0), .en(AddEnable), .reset(Reset));  // open: Qn
  Comparator #(.mode("unsigned")) comparator_1 (.a(adder_1_out), .b({8{1'b0}}), .eq(comparator_1_eq));  // open: gt, lt
  D_Flip_Flop #(.enable("true")) d_ff_2 (
    .clk(Clock), .D(comparator_1_eq), .Q(ZeroFlag), .preset(1'b0), .en(AddEnable), .reset(Reset));  // open: Qn
endmodule

module ProgramCounter (
  input  [7:0] D,
  input  Reset,
  input  Clock,
  input  WriteEnable,
  input  LoadEnable,
  input  ReadEnable,
  output [7:0] ToBus
);

  wire or_1_out;
  wire [3:0] adder_1_out, multiplexer_1_out, register_1_q;
  wire [7:4] undriven;

  Adder #(.width(4)) adder_1 (.a(register_1_q), .b(4'b0000), .out(adder_1_out), .cin(1'b1));  // open: cout
  Multiplexer #(.enable("false"), .width(4)) multiplexer_1 (
    .in0(adder_1_out), .in1(D[3:0]), .out(multiplexer_1_out), .sel(LoadEnable));
  Register #(.width(4)) register_1 (.D(multiplexer_1_out), .en(or_1_out), .Q(register_1_q), .clk(Clock), .clr(Reset));
  or or_1 (or_1_out, LoadEnable, WriteEnable);
  assign ToBus = ReadEnable ? {undriven, register_1_q} : 8'bz;  // Controlled_Buffer controlled_buffer_1
endmodule

module InstructionFetcher (
  input  IRWriteEnable,
  input  [7:0] InstructionIn,
  input  ReadEnable,
  input  Clock,
  input  Reset,
  output [7:0] ToBus,
  output [6:0] ToSignalROM
);

  wire [3:0] IR_q;
  wire [7:4] undriven;

  Register IR (.D(InstructionIn), .en(IRWriteEnable), .Q({ToSignalROM[6:3], IR_q}), .clk(Clock), .clr(Reset));
  Counter #(.max('h4), .width(3)) Step (
    .load(1'b0), .count(1'b1), .Q(ToSignalROM[2:0]), .up(1'b1), .clk(Clock), .clr(Reset));  // open: D, carry
  assign ToBus = ReadEnable ? {undriven, IR_q} : 8'bz;  // Controlled_Buffer controlled_buffer_1
endmodule

module Output (
  input  [7:0] D,
  input  Reset,
  input  Clock,
  input  WriteEnable,
  output [7:0] Out
);

  Register register_1 (.D(D), .en(WriteEnable), .Q(Out), .clk(Clock), .clr(Reset));
endmodule

module AddrRegister (
  input  [7:0] D,
  input  ProgramMode,
  input  [3:0] AddrBypass,
  input  WriteEnable,
  input  Clock,
  input  Reset,
  output [3:0] ToRAM
);

  wire [3:0] Addr_q;

  Register #(.width(4)) Addr (.D(D[3:0]), .en(WriteEnable), .Q(Addr_q), .clk(Clock), .clr(Reset));
  Multiplexer #(.enable("false"), .width(4)) multiplexer_1 (
    .in0(Addr_q), .in1(AddrBypass), .out(ToRAM), .sel(ProgramMode));
endmodule

module CPUClock (
  input  Pulse,
  input  StepMode,
  input  Halt,
  output Clk
);

  wire clock_1_out, not_1_out;

  Clock clock_1 (.out(clock_1_out));
  Multiplexer multiplexer_1 (.in0(clock_1_out), .in1(Pulse), .out(Clk), .sel(StepMode), .en(not_1_out));
  not not_1 (not_1_out, Halt);
endmodule
